# Fritzing sketch scheme (saved by Fritzing 0.9.3b)

parts:
  Часть1 = Arduino Nano (Rev3.0) [part_number="Arduino NANO"]
  WeMos_D1_Mini1 = WeMos D1 Mini
  Часть2 = BluePill [part_number="STM32 Blue Pill"]
  U1 = NodeMCU V3.0 [part_number=NodeMCU]
  Часть3 = Bluetooth HC-06 [part_number="Bluetooth (по желанию)"]
  Часть6 = Bluetooth HC-06 [part_number="Bluetooth по желанию"]
  U197 = mystery part, 1 pin [chip_label=IN1 part_number="Din ленты"]
  S6 = Pushbutton [part_number=Выбор package="[THT]"]
  S7 = Pushbutton [part_number=Низ package="[THT]"]
  S8 = Pushbutton [part_number=Право package="[THT]"]
  S9 = Pushbutton [part_number=Лево package="[THT]"]
  S10 = Pushbutton [part_number=Верх package="[THT]"]
  Часть7 = Bluetooth HC-06 [part_number="Bluetooth (по желанию)"]
  U198 = mystery part, 1 pin [chip_label=IN1 part_number="Din ленты"]
  S11 = Pushbutton [part_number=Выбор package="[THT]"]
  S12 = Pushbutton [part_number=Низ package="[THT]"]
  S13 = Pushbutton [part_number=Право package="[THT]"]
  S14 = Pushbutton [part_number=Лево package="[THT]"]
  S15 = Pushbutton [part_number=Верх package="[THT]"]
  U199 = mystery part, 1 pin [chip_label=IN1 part_number="Din ленты"]
  S16 = Pushbutton [part_number=Лево package="[THT]"]
  S17 = Pushbutton [part_number=Верх package="[THT]"]
  S18 = Pushbutton [part_number=Право package="[THT]"]
  S19 = Pushbutton [part_number=Выбор package="[THT]"]
  S20 = Pushbutton [part_number=Вниз package="[THT]"]
  Часть8 = Bluetooth HC-06 [part_number="Bluetooth (по желанию)"]
  U200 = mystery part, 1 pin [chip_label=IN1 part_number="Din ленты"]
  S21 = Pushbutton [part_number=Выбор package="[THT]"]
  S22 = Pushbutton [part_number=Низ package="[THT]"]
  S23 = Pushbutton [part_number=Право package="[THT]"]
  S24 = Pushbutton [part_number=Лево package="[THT]"]
  S25 = Pushbutton [part_number=Верх package="[THT]"]
  Часть9 = Arduino Mega 2560 (Rev3) [part_number="Arduino MEGA"]
  S26 = Pushbutton [part_number=Выбор package="[THT]"]
  S27 = Pushbutton [part_number=Низ package="[THT]"]
  S28 = Pushbutton [part_number=Право package="[THT]"]
  S29 = Pushbutton [part_number=Лево package="[THT]"]
  S30 = Pushbutton [part_number=Верх package="[THT]"]
  U201 = mystery part, 1 pin [chip_label=IN1 part_number="Din ленты"]
  Часть10 = Bluetooth HC-06 [part_number="Bluetooth (по желанию)"]
  ZS-042_RTC1 = ZS-042 RTC Module [part_number="Модуль часов DS3231 (по желанию)"]
  ZS-042_RTC2 = ZS-042 RTC Module [part_number="Модуль часов DS3231 (по желанию)"]
  ZS-042_RTC3 = ZS-042 RTC Module [part_number="Модуль часов DS3231 (по желанию)"]
  ZS-042_RTC4 = ZS-042 RTC Module [part_number="Модуль часов DS3231 (по желанию)"]
  U202 = mystery part, 1 pin [chip_label=IN1 part_number=5V]  # not connected
  U203 = mystery part, 1 pin [chip_label=IN1 part_number=GND]  # not connected
  U204 = mystery part, 1 pin [chip_label=IN1 part_number=GND]  # not connected
  U205 = mystery part, 1 pin [chip_label=IN1 part_number=5V]  # not connected
  U206 = mystery part, 1 pin [chip_label=IN1 part_number=GND]
  U207 = mystery part, 1 pin [chip_label=IN1 part_number=5V]
  U208 = mystery part, 1 pin [chip_label=IN1 part_number=GND]
  U209 = mystery part, 1 pin [chip_label=IN1 part_number=5V]
  U210 = mystery part, 1 pin [chip_label=IN1 part_number=GND]
  U211 = mystery part, 1 pin [chip_label=IN1 part_number=5V]

nets:
  N1: Часть1.D1/TX, Часть3.RXD
  N2: Часть1.D0/RX, Часть3.TXD
  GND: Часть1.GND, Часть3.GND, S6.Pin_4, S7.Pin_4, S8.Pin_4, S9.Pin_3, S9.Pin_4, S10.Pin_4, ZS-042_RTC1.GND
  N3: Часть1.D2, S9.Pin_1
  N4: Часть1.D3, S10.Pin_1
  N5: Часть1.D4, S8.Pin_1
  N6: Часть1.D5, S7.Pin_1
  N7: Часть1.D6, U197.pin1
  N8: Часть1.D7, S6.Pin_1
  VCC: Часть1.5V, Часть3.VCC, ZS-042_RTC1.VCC
  N9: Часть1.A5, ZS-042_RTC1.SCL
  N10: Часть1.A4, ZS-042_RTC1.SDA
  N11: WeMos_D1_Mini1.3V3, S11.Pin_1
  VCC_2: WeMos_D1_Mini1.5V, Часть7.VCC, ZS-042_RTC2.VCC
  N12: WeMos_D1_Mini1.D1, ZS-042_RTC2.SCL
  N13: WeMos_D1_Mini1.D2, ZS-042_RTC2.SDA
  N14: WeMos_D1_Mini1.D3, S14.Pin_1
  N15: WeMos_D1_Mini1.D4, U198.pin1
  N16: WeMos_D1_Mini1.D5, S15.Pin_1
  N17: WeMos_D1_Mini1.D6, S13.Pin_1
  N18: WeMos_D1_Mini1.D7, S12.Pin_1
  GND_2: WeMos_D1_Mini1.D8, WeMos_D1_Mini1.G, Часть7.GND, S11.Pin_3, S11.Pin_4, S12.Pin_4, S13.Pin_4, S14.Pin_3, S14.Pin_4, S15.Pin_4, ZS-042_RTC2.GND
  N19: WeMos_D1_Mini1.RX, Часть7.TXD
  N20: WeMos_D1_Mini1.TX, Часть7.RXD
  3V3: Часть2.3V3, Часть6.VCC
  GND2: Часть2.GND2, Часть6.GND, S21.Pin_3, S21.Pin_4, S22.Pin_4, S23.Pin_4, S24.Pin_3, S24.Pin_4, S25.Pin_4
  N21: Часть2.GND3, U206.pin1
  N22: Часть2.5V, U207.pin1
  N23: Часть2.A10, Часть6.TXD
  N24: Часть2.A9, Часть6.RXD
  N25: Часть2.B12, U200.pin1
  N26: U1.D1, ZS-042_RTC3.SCL
  N27: U1.D2, ZS-042_RTC3.SDA
  N28: U1.D3, S16.Pin_1, S16.Pin_2
  N29: U1.D4, U199.pin1
  VCC_3: U1.3V3, S19.Pin_3, S19.Pin_4, Часть8.VCC, ZS-042_RTC3.VCC
  GND_3: U1.GND, S16.Pin_4, S17.Pin_4, S18.Pin_4, S20.Pin_3, S20.Pin_4, Часть8.GND, ZS-042_RTC3.GND, U208.pin1
  N30: U1.D5, S17.Pin_1
  N31: U1.D6, S18.Pin_1
  N32: U1.D7, S20.Pin_1
  N33: U1.D8, S19.Pin_1, S19.Pin_2
  N34: U1.RX, Часть8.TXD
  N35: U1.TX, Часть8.RXD
  N36: U1.Vin, U209.pin1
  N37: Часть9.D21/SCL, ZS-042_RTC4.SCL
  N38: Часть9.D20/SDA, ZS-042_RTC4.SDA
  GND_4: Часть9.GND, Часть9.D2_PWM, Часть9.D3_PWM, Часть9.D4_PWM, Часть9.D5_PWM, Часть9.D7_PWM, S26.Pin_1, S26.Pin_2, S27.Pin_1, S27.Pin_2, S28.Pin_1, S28.Pin_2, S28.Pin_3, S29.Pin_1, S29.Pin_2, S30.Pin_1, S30.Pin_2, Часть10.GND, ZS-042_RTC4.GND, U210.pin1
  VCC_4: Часть9.5V, Часть10.VCC, ZS-042_RTC4.VCC, U211.pin1
  N39: Часть9.D0_RX0, Часть10.TXD
  N40: Часть9.D1_TX0, Часть10.RXD
  N41: Часть9.D6_PWM, U201.pin1

custom parts:
  NodeMCU V3.0: ESP8266 based NodeMCU
